// Logisim project additionneur1-Jules.circ as structural Verilog: 6 circuits, main circuit additionneur 4bits
module additionneur_4bits (
  input  [3:0] B,
  input  [3:0] A,
  input  Cin,
  output [3:0] out_4,
  output SP,
  output SG
);

  wire additionneur_1_g, additionneur_1_p, additionneur_2_g, additionneur_2_p, additionneur_3_g,
       additionneur_3_p, additionneur_4_g, additionneur_4_p, \unité_de_calcul_1_1_cout1 ,
       \unité_de_calcul_1_1_cout2 , \unité_de_calcul_1_1_cout3 , \unité_de_calcul_1_1_cout4 ;

  Additionneur additionneur_1 (
    .A(A[0]), .B(B[0]), .Cin(\unité_de_calcul_1_1_cout1 ), .S(out_4[0]), .P(additionneur_1_p),
    .G(additionneur_1_g));
  Additionneur additionneur_2 (
    .A(A[1]), .B(B[1]), .Cin(\unité_de_calcul_1_1_cout2 ), .S(out_4[1]), .P(additionneur_2_p),
    .G(additionneur_2_g));
  Additionneur additionneur_3 (
    .A(A[2]), .B(B[2]), .Cin(\unité_de_calcul_1_1_cout3 ), .S(out_4[2]), .P(additionneur_3_p),
    .G(additionneur_3_g));
  \unité_de_calcul_1  \unité_de_calcul_1_1  (
    .Cin(Cin), .P1(additionneur_1_p), .G1(additionneur_1_g), .P2(additionneur_2_p), .G2(additionneur_2_g),
    .P3(additionneur_3_p), .G3(additionneur_3_g), .P4(additionneur_4_p), .G4(additionneur_4_g),
    .Cout1(\unité_de_calcul_1_1_cout1 ), .Cout2(\unité_de_calcul_1_1_cout2 ),
    .Cout3(\unité_de_calcul_1_1_cout3 ), .Cout4(\unité_de_calcul_1_1_cout4 ), .SP(SP), .SG(SG));  // open: CoutT
  Additionneur additionneur_4 (
    .A(A[3]), .B(B[3]), .Cin(\unité_de_calcul_1_1_cout4 ), .S(out_4[3]), .P(additionneur_4_p),
    .G(additionneur_4_g));
endmodule

module Additionneur (
  input  A,
  input  B,
  input  Cin,
  output S,
  output P,
  output G
);

  wire xor_1_out;

  xor xor_1 (xor_1_out, A, B);
  or or_1 (P, A, B);
  and and_1 (G, A, B);
  xor xor_2 (S, xor_1_out, Cin);
endmodule

module \unité_de_calcul_1  (
  input  Cin,
  input  P1,
  input  G1,
  input  P2,
  input  G2,
  input  P3,
  input  G3,
  input  P4,
  input  G4,
  output Cout3,
  output Cout2,
  output Cout4,
  output Cout1,
  output CoutT,
  output SP,
  output SG
);

  wire and_1_out, and_3_out, and_4_out, and_5_out, and_6_out, and_7_out, and_8_out, and_9_out, and_10_out,
       and_11_out, and_12_out, and_13_out, and_14_out;

  and and_1 (and_1_out, Cin, P1);
  or or_1 (Cout2, and_1_out, G1);
  and and_2 (SP, P1, P2, P3, P4);
  and and_3 (and_3_out, G1, P2, P3, P4);
  and and_4 (and_4_out, G1, P2);
  and and_5 (and_5_out, Cin, P1, P2);
  or or_2 (Cout3, and_5_out, and_4_out, G2);
  and and_6 (and_6_out, G2, P3);
  and and_7 (and_7_out, G2, P3, P4);
  and and_8 (and_8_out, G1, P2, P3);
  and and_9 (and_9_out, P1, Cin, P2, P3);
  or or_3 (Cout4, and_9_out, and_6_out, and_8_out, G3);
  and and_10 (and_10_out, G3, P4);
  or or_4 (SG, and_3_out, and_7_out, and_10_out, G4);
  and and_11 (and_11_out, Cin, P1, P2, P3, P4);
  and and_12 (and_12_out, G3, P4);
  and and_13 (and_13_out, G2, P3, P4);
  and and_14 (and_14_out, G1, P3, P2, P4);
  or or_5 (CoutT, and_11_out, and_13_out, and_14_out, G4, and_12_out);

  assign Cout1 = Cin;
endmodule

module additionneur_16bits (
  input  [15:0] B,
  input  [15:0] A,
  input  Cin,
  output [15:0] S,
  output Cout,
  output SP,
  output SG
);

  wire additionneur_4bits_1_sg, additionneur_4bits_1_sp, additionneur_4bits_2_sg, additionneur_4bits_2_sp,
       additionneur_4bits_3_sg, additionneur_4bits_3_sp, additionneur_4bits_4_sg, additionneur_4bits_4_sp,
       \unité_de_calcul_1_1_cout1 , \unité_de_calcul_1_1_cout2 , \unité_de_calcul_1_1_cout3 ,
       \unité_de_calcul_1_1_cout4 ;

  additionneur_4bits additionneur_4bits_1 (
    .Cin(\unité_de_calcul_1_1_cout1 ), .A(A[3:0]), .B(B[3:0]), .SG(additionneur_4bits_1_sg),
    .SP(additionneur_4bits_1_sp), .out_4(S[15:12]));
  additionneur_4bits additionneur_4bits_2 (
    .Cin(\unité_de_calcul_1_1_cout2 ), .A(A[7:4]), .B(B[7:4]), .SG(additionneur_4bits_2_sg),
    .SP(additionneur_4bits_2_sp), .out_4(S[11:8]));
  additionneur_4bits additionneur_4bits_3 (
    .Cin(\unité_de_calcul_1_1_cout3 ), .A(A[11:8]), .B(B[11:8]), .SG(additionneur_4bits_3_sg),
    .SP(additionneur_4bits_3_sp), .out_4(S[7:4]));
  \unité_de_calcul_1  \unité_de_calcul_1_1  (
    .Cin(Cin), .CoutT(Cout), .P1(additionneur_4bits_1_sp), .G1(additionneur_4bits_1_sg),
    .P2(additionneur_4bits_2_sp), .G2(additionneur_4bits_2_sg), .P3(additionneur_4bits_3_sp),
    .G3(additionneur_4bits_3_sg), .P4(additionneur_4bits_4_sp), .G4(additionneur_4bits_4_sg),
    .Cout1(\unité_de_calcul_1_1_cout1 ), .Cout2(\unité_de_calcul_1_1_cout2 ),
    .Cout3(\unité_de_calcul_1_1_cout3 ), .Cout4(\unité_de_calcul_1_1_cout4 ), .SP(SP), .SG(SG));
  additionneur_4bits additionneur_4bits_4 (
    .Cin(\unité_de_calcul_1_1_cout4 ), .A(A[15:12]), .B(B[15:12]), .SG(additionneur_4bits_4_sg),
    .SP(additionneur_4bits_4_sp), .out_4(S[3:0]));
endmodule

module Soustraction (
  input  [15:0] in_1,
  input  [15:0] in_2,
  input  C,
  input  in_4,
  output [15:0] out_5,
  output out_6
);

  wire or_1_out;
  wire [15:0] multiplexer_1_out, not_1_out;

  Multiplexer #(.width(16), .enable("false")) multiplexer_1 (
    .in0(in_2), .in1(not_1_out), .out(multiplexer_1_out), .sel(C));
  assign not_1_out = ~in_2;  // NOT_Gate not_1, 16 bits wide
  additionneur_16bits additionneur_16bits_1 (
    .B(multiplexer_1_out), .A(in_1), .Cin(or_1_out), .Cout(out_6), .S(out_5));  // open: SP, SG
  or or_1 (or_1_out, C, in_4);
endmodule

module multiplexeur (
  input  [2:0] in_1
);

  Multiplexer #(.select(3), .enable("false")) multiplexer_1 (.sel(in_1));  // open: in0, in1, in2, in3, in4, in5, in6, in7, out
endmodule
