// Logisim project additionneur1.circ as structural Verilog: 4 circuits, main circuit main
module main (
  input  in_1,
  input  in_2,
  input  in_3,
  input  in_4,
  input  in_5,
  input  in_6,
  input  in_7,
  input  in_8,
  input  in_9,
  output out_10,
  output out_11,
  output out_12,
  output out_13,
  output out_14
);

  wire additionneur_1_g, additionneur_1_p, additionneur_2_g, additionneur_2_p, additionneur_3_g,
       additionneur_3_p, additionneur_4_g, additionneur_4_p, \unité_de_calcul_1_1_cout1 ,
       \unité_de_calcul_1_1_cout2 , \unité_de_calcul_1_1_cout3 , \unité_de_calcul_1_1_cout4 ;

  Additionneur additionneur_1 (
    .A(in_5), .B(in_6), .Cin(\unité_de_calcul_1_1_cout1 ), .S(out_11), .P(additionneur_1_p),
    .G(additionneur_1_g));
  Additionneur additionneur_2 (
    .A(in_1), .B(in_3), .Cin(\unité_de_calcul_1_1_cout2 ), .S(out_10), .P(additionneur_2_p),
    .G(additionneur_2_g));
  Additionneur additionneur_3 (
    .A(in_2), .B(in_4), .Cin(\unité_de_calcul_1_1_cout3 ), .S(out_12), .P(additionneur_3_p),
    .G(additionneur_3_g));
  \unité_de_calcul_1  \unité_de_calcul_1_1  (
    .Cin(in_9), .CoutT(out_14), .P1(additionneur_1_g), .G1(additionneur_1_p), .P2(additionneur_2_g),
    .G2(additionneur_2_p), .P3(additionneur_3_g), .G3(additionneur_3_p), .P4(additionneur_4_g),
    .G4(additionneur_4_p), .Cout1(\unité_de_calcul_1_1_cout1 ), .Cout2(\unité_de_calcul_1_1_cout2 ),
    .Cout3(\unité_de_calcul_1_1_cout3 ), .Cout4(\unité_de_calcul_1_1_cout4 ));
  Additionneur additionneur_4 (
    .A(in_7), .B(in_8), .Cin(\unité_de_calcul_1_1_cout4 ), .S(out_13), .P(additionneur_4_p),
    .G(additionneur_4_g));
endmodule

module Additionneur (
  input  A,
  input  B,
  input  Cin,
  output S,
  output P,
  output G
);

  wire xor_1_out;

  xor xor_1 (xor_1_out, A, B);
  or or_1 (P, A, B);
  and and_1 (G, A, B);
  xor xor_2 (S, xor_1_out, Cin);
endmodule

module \unité_calcul_de_retenue  (
  input  Cin,
  input  P1,
  input  G1,
  input  P2,
  input  G2,
  input  P3,
  input  G3,
  input  P4,
  input  G4,
  output Cout2,
  output Cout3,
  output Cout4,
  output Cout1,
  output CoutT
);

  wire and_1_out, and_2_out, and_3_out, and_4_out;

  and and_1 (and_1_out, Cin, P1);
  or or_1 (Cout2, and_1_out, G1);
  and and_2 (and_2_out, Cout2, P2);
  or or_2 (Cout3, and_2_out, G2);
  and and_3 (and_3_out, Cout3, P3);
  or or_3 (Cout4, and_3_out, G3);
  and and_4 (and_4_out, Cout4, P4);
  or or_4 (CoutT, and_4_out, G4);

  assign Cout1 = Cin;
endmodule

module \unité_de_calcul_1  (
  input  Cin,
  input  P1,
  input  G1,
  input  P2,
  input  G2,
  input  P3,
  input  G3,
  input  P4,
  input  G4,
  output Cout3,
  output Cout2,
  output Cout4,
  output Cout1,
  output CoutT
);

  wire and_1_out, and_2_out, and_3_out, and_4_out, and_5_out, and_6_out, and_7_out, and_8_out, and_9_out,
       and_10_out;

  and and_1 (and_1_out, Cin, P1);
  or or_1 (Cout2, and_1_out, G1);
  and and_2 (and_2_out, P1, P2);
  and and_3 (and_3_out, Cin, P1, P2);
  or or_2 (Cout3, and_3_out, and_2_out, G2);
  and and_4 (and_4_out, G2, P3);
  and and_5 (and_5_out, G1, P2, P3);
  and and_6 (and_6_out, P1, Cin, P2, P3);
  or or_3 (Cout4, and_6_out, and_4_out, and_5_out, G3);
  and and_7 (and_7_out, Cin, P1, P2, P3, P4);
  and and_8 (and_8_out, G3, P4);
  and and_9 (and_9_out, G2, P3, P4);
  and and_10 (and_10_out, G1, P3, P2, P4);
  or or_4 (CoutT, and_7_out, and_9_out, and_10_out, G4, and_8_out);

  assign Cout1 = Cin;
endmodule
